// Logisim project NSU-2022-T04L1e04.circ as structural Verilog: 1 circuit, main circuit mycircuit
module mycircuit (
  input  A,
  input  B,
  input  C,
  output R
);

  wire or_1_out;

  or or_1 (or_1_out, B, C);
  and and_1 (R, ~A, or_1_out);  // AND_Gate
endmodule
