// Logisim project NSU-2022-T04L1e05.circ as structural Verilog: 1 circuit, main circuit mycircuit
module mycircuit (
  input  A,
  input  B,
  input  C,
  output R
);

  or or_1 (R, ~A, ~B, ~C);  // OR_Gate
endmodule
