// Logisim project NSU-2022-T04L1e06.circ as structural Verilog: 1 circuit, main circuit mycircuit
module mycircuit (
  input  A,
  input  B,
  input  C,
  output R
);

  xnor even_parity_1 (R, A, B);
endmodule
