// Logisim project NSU-2022-T04L1e07.circ as structural Verilog: 1 circuit, main circuit mycircuit
module mycircuit (
  input  A,
  input  B,
  input  C,
  output R
);

  wire even_parity_1_out, xor_1_out;

  xnor even_parity_1 (even_parity_1_out, A, C);
  xor xor_1 (xor_1_out, B, C);
  and and_1 (R, even_parity_1_out, xor_1_out);
endmodule
