// Logisim project NSU-2022-T04L1e13.circ as structural Verilog: 1 circuit, main circuit mycircuit
module mycircuit (
  input  A,
  input  B,
  input  C,
  output R
);

  wire and_1_out;

  and and_1 (and_1_out, B, C);
  or or_1 (R, A, and_1_out);

  // Notes on the sheet:
  //   В и С подняты - иначе следует за А
endmodule
