// Logisim project NSU-2022-T04L2e01.circ as structural Verilog: 1 circuit, main circuit OR3
module OR3 (
  input  A,
  input  B,
  input  C,
  output R
);

  wire transistor_5_out, transistor_6_out;

  Transistor #(.\type ("n")) transistor_1 (.in(1'b0), .out(R), .gate(A));
  Transistor #(.\type ("n")) transistor_2 (.in(1'b0), .out(R), .gate(B));
  Transistor #(.\type ("n")) transistor_3 (.in(1'b0), .out(R), .gate(C));
  Transistor transistor_4 (.in(transistor_5_out), .out(R), .gate(A));
  Transistor transistor_5 (.in(transistor_6_out), .out(transistor_5_out), .gate(B));
  Transistor #(.gate("br")) transistor_6 (.in(1'b1), .out(transistor_6_out), .gate(C));

  // Notes on the sheet:
  //   NOR
endmodule
