// Logisim project NSU-2022-T04L2e02.circ as structural Verilog: 1 circuit, main circuit formula
module formula (
  input  A,
  input  B,
  input  C,
  output R
);

  wire pull_resistor_1_node, transistor_1_out;

  Transistor transistor_1 (.in(C), .out(transistor_1_out), .gate(B));
  Pull_Resistor pull_resistor_1 (.node(pull_resistor_1_node));
  Transistor #(.\type ("n"), .gate("br")) transistor_2 (.in(A), .out(pull_resistor_1_node), .gate(transistor_1_out));
  Pull_Resistor #(.pull(1)) pull_resistor_2 (.node(transistor_1_out));
  Transistor transistor_3 (.in(1'b1), .out(R), .gate(pull_resistor_1_node));
  Pull_Resistor pull_resistor_3 (.node(R));

  // Notes on the sheet:
  //   OR
  //   R = NOT(A AND (B OR C))
  //   and
  //   not
endmodule
