// Logisim project NSU-2022-T05L1e09.circ as structural Verilog: 4 circuits, main circuit main
module main (
  input  [7:0] u,
  input  [7:0] v,
  output [7:0] R
);

  wire not_3_out, not_4_out;
  wire [7:0] inc_2_r, inc_3_r, mux_2_output, not_1_out, not_2_out, undriven;

  inc inc_1 ();  // open: X, R, Cout
  // Probe on u
  // Probe on v
  assign not_1_out = ~v;  // NOT_Gate not_1, 8 bits wide
  // Probe on v[7]
  inc inc_2 (.X(not_1_out), .R(inc_2_r));  // open: Cout
  // Probe on inc_2_r
  MUX mux_1 ();  // open: Input_0, sel, Input_1, Output
  MUX mux_2 (.Input_0(v), .sel(v[7]), .Input_1(inc_2_r), .Output(mux_2_output));
  // Probe on mux_2_output
  // Probe on R
  add add_1 (.A(u), .B(mux_2_output), .sum(R));  // open: Cout, Cin
  assign not_2_out = ~undriven;  // NOT_Gate not_2, 8 bits wide
  add add_2 ();  // open: A, B, sum, Cout, Cin
  // Probe on R
  // Probe on inc_3_r
  inc inc_3 (.X(not_2_out), .R(inc_3_r));  // open: Cout
  not not_3 (not_3_out, undriven[7]);
  // Probe on undriven[7]
  not not_4 (not_4_out, not_4_out);
  MUX if_1___A_else_B (.Input_0(inc_3_r), .sel(not_3_out), .Input_1(undriven));  // open: Output
  // NOT_Gate not_5 is placed but not wired
  // OR_Gate or_1 is placed but not wired
  // OR_Gate or_2 is placed but not wired
  // Probe on R
  // AND_Gate and_1 is placed but not wired
  // AND_Gate and_2 is placed but not wired
  // XOR_Gate xor_1 is placed but not wired
  // XOR_Gate xor_2 is placed but not wired
  // XNOR_Gate xnor_1 is placed but not wired

  // Notes on the sheet:
  //   signed decimal:
  //   BOTH INPUTS use 2's comp
  //   signed decimal:
  //   split a bunch into 8 individual wires
  //   all the above are 8-bit devices
  //   You are only allowed to use Wiring and Gates libraries
  //   Chips you may use in addition to gates (Click and Ctrl/D duplicates):
  //   You may also use the following (and any other)  splitters facing any direction
  //   ATTENTION! DO NOT MOVE ANY PINS!
  //   Ignore overflow, unless instructed otherwise
  //   You may build and use your own chips using gates and wires
  //   R = u + |v|
  //   out = A if sel=0
  //   B if sel=1
  //   extract the sign bit (bit 7) from an 8-bit bunch
  //   extract the LSB  (bit 0) from an 8-bit bunch
  //   constant 8-bit value (change it to anything  you want)
  //   Cin pulled to 0 if disconnected
  //   signed decimal:
  //   Gates: Click and Ctrl/D duplicates
  //   You may use any gates, not just the above ones
endmodule

module inc (
  input  [7:0] X,
  output [7:0] R,
  output Cout
);

  wire [7:1] and_1_out;

  assign {Cout, and_1_out} = {and_1_out, 1'b1} & X;  // AND_Gate and_1, 8 bits wide
  assign R = X ^ {and_1_out, 1'b1};  // XOR_Gate xor_1, 8 bits wide
endmodule

module add (
  input  [7:0] A,
  input  [7:0] B,
  input  Cin,
  output [7:0] sum,
  output Cout
);

  wire [6:0] or_1_out;
  wire [7:0] and_1_out, and_2_out, and_3_out;

  Pull_Resistor pull_resistor_1 (.node(Cin));
  assign and_1_out = A & B;  // AND_Gate and_1, 8 bits wide
  assign and_2_out = B & {or_1_out, Cin};  // AND_Gate and_2, 8 bits wide
  assign and_3_out = A & {or_1_out, Cin};  // AND_Gate and_3, 8 bits wide
  assign {Cout, or_1_out} = and_1_out | and_2_out | and_3_out;  // OR_Gate or_1, 8 bits wide
  assign sum = A ^ {or_1_out, Cin} ^ B;  // XOR_Gate xor_1, 8 bits wide
endmodule

module MUX (
  input  [7:0] Input_0,
  input  sel,
  input  [7:0] Input_1,
  output [7:0] Output
);

  wire [7:0] and_1_out, and_2_out;
  wire [7:7] not_1_out;

  not not_1 (not_1_out[7], sel);
  assign and_1_out = Input_0 & {8{not_1_out[7]}};  // AND_Gate and_1, 8 bits wide
  assign and_2_out = {8{sel}} & Input_1;  // AND_Gate and_2, 8 bits wide
  assign Output = and_1_out | and_2_out;  // OR_Gate or_1, 8 bits wide
endmodule
