// Logisim project NSU-2022-T05L1e10.circ as structural Verilog: 4 circuits, main circuit main
module main (
  input  [7:0] u,
  input  [7:0] v,
  output [7:0] R
);

  wire not_5_out, not_6_out;
  wire [7:0] inc_2_r, inc_3_r, inc_4_r, inc_5_r, inc_6_r, inc_7_r, mux_2_output, mux_3_output, mux_4_output,
       mux_5_output, not_1_out, not_2_out, not_3_out, not_4_out;

  inc inc_1 ();  // open: X, R, Cout
  // Probe on u
  // Probe on v
  assign not_1_out = ~u;  // NOT_Gate not_1, 8 bits wide
  assign not_2_out = ~u;  // NOT_Gate not_2, 8 bits wide
  // Probe on u[0]
  inc inc_2 (.X(not_1_out), .R(inc_2_r));  // open: Cout
  inc inc_3 (.X(not_2_out), .R(inc_3_r));  // open: Cout
  MUX mux_1 ();  // open: Input_0, sel, Input_1, Output
  MUX mux_2 (.Input_0({8{1'b0}}), .sel(u[0]), .Input_1(8'h1), .Output(mux_2_output));
  // Probe on {1'b0, inc_2_r[7:1]}
  // Probe on {1'b0, inc_3_r[7:1]}
  // Probe on u[0]
  // Probe on u[0]
  // Probe on u[0]
  MUX mux_3 (.Input_0({8{1'b0}}), .sel(u[0]), .Input_1(8'h1), .Output(mux_3_output));
  inc inc_4 (.X({1'b0, inc_2_r[7:1]}), .R(inc_4_r));  // open: Cout
  // Probe on inc_4_r
  inc inc_5 (.X({1'b0, inc_3_r[7:1]}), .R(inc_5_r));  // open: Cout
  // Probe on inc_5_r
  MUX mux_4 (.Input_0({1'b0, inc_2_r[7:1]}), .sel(u[0]), .Input_1(inc_4_r), .Output(mux_4_output));
  MUX mux_5 (.Input_0({1'b0, inc_3_r[7:1]}), .sel(u[0]), .Input_1(inc_5_r), .Output(mux_5_output));
  add add_1 ();  // open: A, B, sum, Cout, Cin
  // Probe on u[7]
  assign not_3_out = ~mux_4_output;  // NOT_Gate not_3, 8 bits wide
  // Probe on mux_4_output
  // Probe on mux_5_output
  assign not_4_out = ~mux_5_output;  // NOT_Gate not_4, 8 bits wide
  // Probe on u[7]
  inc inc_6 (.X(not_3_out), .R(inc_6_r));  // open: Cout
  inc inc_7 (.X(not_4_out), .R(inc_7_r));  // open: Cout
  // Probe on inc_7_r
  not not_5 (not_5_out, u[7]);
  // Probe on mux_3_output
  not not_6 (not_6_out, not_6_out);
  // Probe on mux_2_output
  // Probe on inc_6_r
  MUX mux_6 (.Input_0(mux_2_output), .sel(u[7]), .Input_1(inc_6_r), .Output(R));
  MUX mux_7 (.Input_0(inc_7_r), .sel(not_5_out), .Input_1(mux_3_output));  // open: Output
  // NOT_Gate not_7 is placed but not wired
  // OR_Gate or_1 is placed but not wired
  // OR_Gate or_2 is placed but not wired
  // Probe on R
  // AND_Gate and_1 is placed but not wired
  // AND_Gate and_2 is placed but not wired
  // XOR_Gate xor_1 is placed but not wired
  // XOR_Gate xor_2 is placed but not wired
  // XNOR_Gate xnor_1 is placed but not wired

  // Other names for the same wires on the sheet: x[7:0] = u

  // Notes on the sheet:
  //   signed decimal:
  //   BOTH INPUTS use 2's comp
  //   ИГНОР
  //   signed decimal:
  //   split a bunch into 8 individual wires
  //   all the above are 8-bit devices
  //   деление: вычисление остатка
  //   деление: вычисление целой части
  //   You are only allowed to use Wiring and Gates libraries
  //   Chips you may use in addition to gates (Click and Ctrl/D duplicates):
  //   You may also use the following (and any other)  splitters facing any direction
  //   ATTENTION! DO NOT MOVE ANY PINS!
  //   Ignore overflow, unless instructed otherwise
  //   You may build and use your own chips using gates and wires
  //   if u < 0 then R = u/2 else R = u mod 2
  //   out = A if sel=0
  //   B if sel=1
  //   первая версия
  //   extract the sign bit (bit 7) from an 8-bit bunch
  //   extract the LSB  (bit 0) from an 8-bit bunch
  //   constant 8-bit value (change it to anything  you want)
  //   Cin pulled to 0 if disconnected
  //   signed decimal:
  //   Gates: Click and Ctrl/D duplicates
  //   You may use any gates, not just the above ones
endmodule

module inc (
  input  [7:0] X,
  output [7:0] R,
  output Cout
);

  wire [7:1] and_1_out;

  assign {Cout, and_1_out} = {and_1_out, 1'b1} & X;  // AND_Gate and_1, 8 bits wide
  assign R = X ^ {and_1_out, 1'b1};  // XOR_Gate xor_1, 8 bits wide
endmodule

module add (
  input  [7:0] A,
  input  [7:0] B,
  input  Cin,
  output [7:0] sum,
  output Cout
);

  wire [6:0] or_1_out;
  wire [7:0] and_1_out, and_2_out, and_3_out;

  Pull_Resistor pull_resistor_1 (.node(Cin));
  assign and_1_out = A & B;  // AND_Gate and_1, 8 bits wide
  assign and_2_out = B & {or_1_out, Cin};  // AND_Gate and_2, 8 bits wide
  assign and_3_out = A & {or_1_out, Cin};  // AND_Gate and_3, 8 bits wide
  assign {Cout, or_1_out} = and_1_out | and_2_out | and_3_out;  // OR_Gate or_1, 8 bits wide
  assign sum = A ^ {or_1_out, Cin} ^ B;  // XOR_Gate xor_1, 8 bits wide
endmodule

module MUX (
  input  [7:0] Input_0,
  input  sel,
  input  [7:0] Input_1,
  output [7:0] Output
);

  wire [7:0] and_1_out, and_2_out;
  wire [7:7] not_1_out;

  not not_1 (not_1_out[7], sel);
  assign and_1_out = Input_0 & {8{not_1_out[7]}};  // AND_Gate and_1, 8 bits wide
  assign and_2_out = {8{sel}} & Input_1;  // AND_Gate and_2, 8 bits wide
  assign Output = and_1_out | and_2_out;  // OR_Gate or_1, 8 bits wide
endmodule
