// Logisim project NSU-2022-T05L2e01.circ as structural Verilog: 1 circuit, main circuit inc
module inc (
  input  [7:0] X,
  output [7:0] R,
  output Cout
);

  wire [6:0] and_1_out;

  // Probe on X
  // Probe on {and_1_out, 1'b1}
  // Probe on X
  // Probe on X
  // Probe on {and_1_out, 1'b1}
  assign {Cout, and_1_out} = {and_1_out, 1'b1} & X;  // AND_Gate and_1, 8 bits wide
  // Probe on {Cout, and_1_out}
  assign R = X ^ {and_1_out, 1'b1};  // XOR_Gate xor_1, 8 bits wide
  // Probe on R

  // Notes on the sheet:
  //   ИНКРЕМЕНТАТОР
endmodule
