// Logisim project NSU-2022-T05L2e02.circ as structural Verilog: 1 circuit, main circuit dec
module dec (
  input  [7:0] X,
  output [7:0] R,
  output Cout
);

  wire [7:1] or_1_out;

  // Probe on X
  assign {Cout, or_1_out} = {or_1_out, 1'b0} | X;  // OR_Gate or_1, 8 bits wide
  assign R = ~(X ^ {or_1_out, 1'b0});  // XNOR_Gate xnor_1, 8 bits wide
  // Probe on R

  // Notes on the sheet:
  //   ДЕКРЕМЕНТАТОР
endmodule
