// Logisim project NSU-2022-T05L2e03.circ as structural Verilog: 2 circuits, main circuit formula
module formula (
  input  [7:0] A,
  output [7:0] R,
  output OFL
);

  wire sum_1_cout;

  // Probe on A
  SUM sum_1 (.A(A), .sum(R), .B({A[5:0], 2'b00}), .Cout(sum_1_cout));  // open: Cin
  or or_1 (OFL, sum_1_cout, A[6], A[7]);
  // Probe on R
  // Probe on OFL
endmodule

module SUM (
  input  [7:0] A,
  input  [7:0] B,
  input  Cin,
  output [7:0] sum,
  output Cout
);

  wire [6:0] or_1_out;
  wire [7:0] and_1_out, and_2_out, and_3_out;

  assign and_1_out = A & B;  // AND_Gate and_1, 8 bits wide
  assign and_2_out = B & {or_1_out, Cin};  // AND_Gate and_2, 8 bits wide
  assign and_3_out = A & {or_1_out, Cin};  // AND_Gate and_3, 8 bits wide
  assign {Cout, or_1_out} = and_1_out | and_2_out | and_3_out;  // OR_Gate or_1, 8 bits wide
  assign sum = A ^ {or_1_out, Cin} ^ B;  // XOR_Gate xor_1, 8 bits wide
  // also tied to GND on the sheet: Cin
endmodule
