// Logisim project NSU-2022-T05L2e04 (НОРМАЛЬНОЕ ЧЕЛОВЕЧЕСКОЕ УМНОЖЕНИЕ НЕ ПРОХОДИТ ТЕСТЫ).circ as structural Verilog: 7 circuits, main circuit mult4x4
module mult4x4 (
  input  [3:0] A,
  input  [3:0] B,
  output [7:0] R
);

  wire xnor_1_out;
  wire [3:0] _2A, _2B, not_1_out, not_2_out, \икрементор_1_r , \икрементор_2_r , \модуль_и_1_out_3 ,
       \модуль_и_2_out_3 , \модуль_и_3_out_3 , \модуль_и_4_out_3 ;
  wire [7:0] not_3_out, \инкрементор8_1_r , \сумматор_1_sum , \сумматор_2_sum , \сумматор_3_sum ;

  assign not_1_out = ~A;  // NOT_Gate not_1, 4 bits wide
  \Икрементор  \u_икрементор_1  (.X(not_1_out), .R(\икрементор_1_r ));  // open: Cout
  assign not_2_out = ~B;  // NOT_Gate not_2, 4 bits wide
  // Probe on A
  // Probe on B
  \МУКС  \u_мукс_1  (.Input_0(A), .sel(A[3]), .Input_1(\икрементор_1_r ), .Output(_2A));
  // Probe on _2A
  \Икрементор  \u_икрементор_2  (.X(not_2_out), .R(\икрементор_2_r ));  // open: Cout
  \МУКС  \u_мукс_2  (.Input_0(B), .sel(B[3]), .Input_1(\икрементор_2_r ), .Output(_2B));
  // Probe on _2B
  \Модуль_И  \u_модуль_и_1  (.in_1(_2A), .in_2(_2B[0]), .out_3(\модуль_и_1_out_3 ));
  \Модуль_И  \u_модуль_и_2  (.in_1(_2A), .in_2(_2B[1]), .out_3(\модуль_и_2_out_3 ));
  \Модуль_И  \u_модуль_и_3  (.in_1(_2A), .in_2(_2B[2]), .out_3(\модуль_и_3_out_3 ));
  \Модуль_И  \u_модуль_и_4  (.in_1(_2A), .in_2(_2B[3]), .out_3(\модуль_и_4_out_3 ));
  \МУКС  \u_мукс_3  ();  // open: Input_0, sel, Input_1, Output
  \МУКС8  \u_мукс8_1  ();  // open: Input_0, sel, Input_1, Output
  // Probe on {4'b0000, \модуль_и_1_out_3 }
  // Probe on {3'b000, \модуль_и_2_out_3 , 1'b0}
  // Probe on {2'b00, \модуль_и_3_out_3 , 2'b00}
  // Probe on {1'b0, \модуль_и_4_out_3 , 3'b000}
  \сумматор  \u_сумматор_1  (
    .A({4'b0000, \модуль_и_1_out_3 }), .B({3'b000, \модуль_и_2_out_3 , 1'b0}), .sum(\сумматор_1_sum ));
  // Probe on \сумматор_1_sum 
  \сумматор  \u_сумматор_2  (.A(\сумматор_1_sum ), .B({2'b00, \модуль_и_3_out_3 , 2'b00}), .sum(\сумматор_2_sum ));
  // Probe on \сумматор_2_sum 
  // Probe on \сумматор_3_sum 
  \сумматор  \u_сумматор_3  (.A(\сумматор_2_sum ), .B({1'b0, \модуль_и_4_out_3 , 3'b000}), .sum(\сумматор_3_sum ));
  assign not_3_out = ~\сумматор_3_sum ;  // NOT_Gate not_3, 8 bits wide
  \Инкрементор8  \u_инкрементор8_1  (.X(not_3_out), .R(\инкрементор8_1_r ));  // open: Cout
  xnor xnor_1 (xnor_1_out, A[3], B[3]);
  \МУКС8  \u_мукс8_2  (.Input_0(\инкрементор8_1_r ), .sel(xnor_1_out), .Input_1(\сумматор_3_sum ), .Output(R));
  // Probe on R

  // Other names for the same wires on the sheet: _1A[3:0] = A; _1B[3:0] = B

  // Notes on the sheet:
  //   Число А
  //   Делает число положительным
  //   Число В
  //   если sel = 0, тогда R = A, иначе R = B
  //   Устанавливает знак
endmodule

module \Модуль_И  (
  input  [3:0] in_1,
  input  in_2,
  output [3:0] out_3
);

  and and_1 (out_3[0], in_1[0], in_2);
  and and_2 (out_3[1], in_1[1], in_2);
  and and_3 (out_3[2], in_1[2], in_2);
  and and_4 (out_3[3], in_1[3], in_2);

  // Other names for the same wires on the sheet: _0A = in_1[0]; _1A = in_1[1]; _2A = in_1[2]; _3A = in_1[3]; B = in_2
endmodule

module \сумматор  (
  input  [7:0] A,
  input  [7:0] B,
  output [7:0] sum
);

  wire [7:0] and_1_out, and_2_out, and_3_out, or_1_out;

  // Probe on A
  // Probe on B
  assign and_1_out = A & B;  // AND_Gate and_1, 8 bits wide
  assign and_2_out = B & {or_1_out[6:0], 1'b0};  // AND_Gate and_2, 8 bits wide
  assign and_3_out = A & {or_1_out[6:0], 1'b0};  // AND_Gate and_3, 8 bits wide
  assign or_1_out = and_1_out | and_2_out | and_3_out;  // OR_Gate or_1, 8 bits wide
  assign sum = A ^ {or_1_out[6:0], 1'b0} ^ B;  // XOR_Gate xor_1, 8 bits wide
  // Probe on sum
endmodule

module \МУКС  (
  input  [3:0] Input_0,
  input  sel,
  input  [3:0] Input_1,
  output [3:0] Output
);

  wire [3:0] and_1_out, and_2_out;
  wire [3:3] not_1_out;

  not not_1 (not_1_out[3], sel);
  assign and_1_out = Input_0 & {4{not_1_out[3]}};  // AND_Gate and_1, 4 bits wide
  assign and_2_out = {4{sel}} & Input_1;  // AND_Gate and_2, 4 bits wide
  assign Output = and_1_out | and_2_out;  // OR_Gate or_1, 4 bits wide
endmodule

module \Икрементор  (
  input  [3:0] X,
  output [3:0] R,
  output Cout
);

  wire [3:1] and_1_out;

  assign {Cout, and_1_out} = {and_1_out, 1'b1} & X;  // AND_Gate and_1, 4 bits wide
  assign R = X ^ {and_1_out, 1'b1};  // XOR_Gate xor_1, 4 bits wide
endmodule

module \МУКС8  (
  input  [7:0] Input_0,
  input  sel,
  input  [7:0] Input_1,
  output [7:0] Output
);

  wire [7:0] and_1_out, and_2_out;
  wire [7:7] not_1_out;

  not not_1 (not_1_out[7], sel);
  assign and_1_out = Input_0 & {8{not_1_out[7]}};  // AND_Gate and_1, 8 bits wide
  assign and_2_out = {8{sel}} & Input_1;  // AND_Gate and_2, 8 bits wide
  assign Output = and_1_out | and_2_out;  // OR_Gate or_1, 8 bits wide
endmodule

module \Инкрементор8  (
  input  [7:0] X,
  output [7:0] R,
  output Cout
);

  wire [7:1] and_1_out;

  assign {Cout, and_1_out} = {and_1_out, 1'b1} & X;  // AND_Gate and_1, 8 bits wide
  assign R = X ^ {and_1_out, 1'b1};  // XOR_Gate xor_1, 8 bits wide
endmodule
