// Logisim project NSU-2022-T05L2e04.circ as structural Verilog: 3 circuits, main circuit mult4x4
module mult4x4 (
  input  [3:0] A,
  input  [3:0] B,
  output [7:0] R
);

  wire [3:0] \модуль_и_1_out_3 , \модуль_и_2_out_3 , \модуль_и_3_out_3 , \модуль_и_4_out_3 ;
  wire [7:0] \сумматор_1_sum , \сумматор_2_sum ;

  // Probe on A
  // Probe on B
  \Модуль_И  \u_модуль_и_1  (.in_1(A), .in_2(B[0]), .out_3(\модуль_и_1_out_3 ));
  \Модуль_И  \u_модуль_и_2  (.in_1(A), .in_2(B[1]), .out_3(\модуль_и_2_out_3 ));
  \Модуль_И  \u_модуль_и_3  (.in_1(A), .in_2(B[2]), .out_3(\модуль_и_3_out_3 ));
  \Модуль_И  \u_модуль_и_4  (.in_1(A), .in_2(B[3]), .out_3(\модуль_и_4_out_3 ));
  // Probe on {4'b0000, \модуль_и_1_out_3 }
  // Probe on {3'b000, \модуль_и_2_out_3 , 1'b0}
  // Probe on {2'b00, \модуль_и_3_out_3 , 2'b00}
  // Probe on {1'b0, \модуль_и_4_out_3 , 3'b000}
  \сумматор  \u_сумматор_1  (
    .A({4'b0000, \модуль_и_1_out_3 }), .B({3'b000, \модуль_и_2_out_3 , 1'b0}), .sum(\сумматор_1_sum ));
  // Probe on \сумматор_1_sum 
  \сумматор  \u_сумматор_2  (.A(\сумматор_1_sum ), .B({2'b00, \модуль_и_3_out_3 , 2'b00}), .sum(\сумматор_2_sum ));
  // Probe on \сумматор_2_sum 
  \сумматор  \u_сумматор_3  (.A(\сумматор_2_sum ), .B({1'b0, \модуль_и_4_out_3 , 3'b000}), .sum(R));
  // Probe on R
  // Probe on R

  // Other names for the same wires on the sheet: _1A[3:0] = A; _1B[3:0] = B
endmodule

module \Модуль_И  (
  input  [3:0] in_1,
  input  in_2,
  output [3:0] out_3
);

  and and_1 (out_3[0], in_1[0], in_2);
  and and_2 (out_3[1], in_1[1], in_2);
  and and_3 (out_3[2], in_1[2], in_2);
  and and_4 (out_3[3], in_1[3], in_2);

  // Other names for the same wires on the sheet: _0A = in_1[0]; _1A = in_1[1]; _2A = in_1[2]; _3A = in_1[3]; B = in_2
endmodule

module \сумматор  (
  input  [7:0] A,
  input  [7:0] B,
  output [7:0] sum
);

  wire [7:0] and_1_out, and_2_out, and_3_out, or_1_out;

  // Probe on A
  // Probe on B
  assign and_1_out = A & B;  // AND_Gate and_1, 8 bits wide
  assign and_2_out = B & {or_1_out[6:0], 1'b0};  // AND_Gate and_2, 8 bits wide
  assign and_3_out = A & {or_1_out[6:0], 1'b0};  // AND_Gate and_3, 8 bits wide
  assign or_1_out = and_1_out | and_2_out | and_3_out;  // OR_Gate or_1, 8 bits wide
  assign sum = A ^ {or_1_out[6:0], 1'b0} ^ B;  // XOR_Gate xor_1, 8 bits wide
  // Probe on sum
endmodule
