// Logisim project NSU-2022-T05L2e05.circ as structural Verilog: 2 circuits, main circuit bcd2
module bcd2 (
  input  Cin,
  input  [7:0] A,
  input  [7:0] B,
  output [7:0] R,
  output Cout
);

  wire bcd_add_1_cout;

  Hex_Digit_Display hex_digit_display_1 (.value(A[7:4]));  // open: dp
  Hex_Digit_Display hex_digit_display_2 (.value(B[7:4]));  // open: dp
  Hex_Digit_Display hex_digit_display_3 (.value({3'b000, Cin}));  // open: dp
  Hex_Digit_Display hex_digit_display_4 (.value(A[3:0]));  // open: dp
  // Probe on A[3:0]
  // Probe on A[7:4]
  Hex_Digit_Display hex_digit_display_5 (.value(B[3:0]));  // open: dp
  // Probe on B[3:0]
  // Probe on B[7:4]
  // Probe on A[3:0]
  // Probe on B[3:0]
  // Probe on A[7:4]
  // Probe on B[7:4]
  bcd_add bcd_add_1 (.Cin(Cin), .A(A[3:0]), .B(B[3:0]), .A_2(R[3:0]), .Cout(bcd_add_1_cout));
  // Probe on R[3:0]
  // Probe on R[7:4]
  bcd_add bcd_add_2 (.Cin(bcd_add_1_cout), .A(A[7:4]), .B(B[7:4]), .A_2(R[7:4]), .Cout(Cout));
  Hex_Digit_Display hex_digit_display_6 (.value({3'b000, Cout}));  // open: dp
  Hex_Digit_Display hex_digit_display_7 (.value(R[7:4]));  // open: dp
  Hex_Digit_Display hex_digit_display_8 (.value(R[3:0]));  // open: dp
  // Probe on R

  // Notes on the sheet:
  //   в 16-ричной системе
  //   в 16-ричной системе
endmodule

// BCD
module bcd_add (
  input  Cin,
  input  [3:0] A,
  input  [3:0] B,
  output [3:0] A_2,
  output Cout
);

  wire comparator_1_gt;
  wire [3:0] adder_1_out, adder_2_out;
  wire [4:4] adder_1_cout;

  // Probe on Cin
  // Probe on A
  // Probe on B
  // Probe on adder_1_out
  Adder #(.width(4)) adder_1 (.a(A), .b(B), .out(adder_1_out), .cin(Cin), .cout(adder_1_cout[4]));
  // Probe on {adder_1_cout[4], adder_1_out}
  Adder #(.width(5)) adder_2 (
    .a({adder_1_cout[4], adder_1_out}), .b(5'b00110), .out({Cout, adder_2_out}));  // open: cin, cout
  // Probe on {adder_1_cout[4], adder_1_out}
  Comparator #(.width(5), .mode("unsigned")) comparator_1 (
    .a({adder_1_cout[4], adder_1_out}), .b(5'b01001), .gt(comparator_1_gt));  // open: eq, lt
  // Probe on adder_1_out
  // Probe on A_2
  Multiplexer #(.width(4)) multiplexer_1 (
    .in0(adder_1_out), .in1(adder_2_out), .out(A_2), .sel(comparator_1_gt));  // open: en
  // Probe on adder_2_out

  // Notes on the sheet:
  //   отвечает за перенос
endmodule
