// Logisim project NSU-2022-T05L3e01.circ as structural Verilog: 3 circuits, main circuit ALU
module ALU (
  input  Cin,
  input  [7:0] A,
  input  [7:0] B,
  input  [1:0] instr,
  output [7:0] R,
  output Cout,
  output V
);

  wire comparator_1_eq, comparator_1_gt, comparator_2_eq, comparator_2_lt, multiplexer_2_out,
       multiplexer_4_out, tunnel, tunnel_t;
  wire [7:0] \И_out , \ИЛИ_out ;

  // Probe on A
  // Probe on B
  // Probe on instr
  assign \И_out  = A & B;  // AND_Gate И, 8 bits wide
  assign \ИЛИ_out  = B | A;  // OR_Gate ИЛИ, 8 bits wide
  Comparator #(.width(2)) comparator_1 (.a(2'b01), .b(instr), .gt(comparator_1_gt), .eq(comparator_1_eq));  // open: lt
  Comparator #(.width(2)) comparator_2 (.a(instr), .b(2'b10), .eq(comparator_2_eq), .lt(comparator_2_lt));  // open: gt
  Adder adder_1 (.a(A), .b(B), .cin(Cin));  // open: out, cout
  Multiplexer #(.enable("false")) multiplexer_1 ();  // open: in0, in1, out, sel
  Multiplexer #(.enable("false")) multiplexer_2 (
    .in1(tunnel_t), .out(multiplexer_2_out), .sel(comparator_2_lt));  // open: in0
  Multiplexer #(.enable("false")) multiplexer_3 (
    .in0(multiplexer_2_out), .in1(tunnel), .out(Cout), .sel(comparator_2_eq));
  Multiplexer #(.enable("false")) multiplexer_4 (.out(multiplexer_4_out));  // open: in0, in1, sel
  Multiplexer #(.enable("false")) multiplexer_5 (.in0(multiplexer_4_out));  // open: in1, out, sel
  Pull_Resistor pull_resistor_1 (.node(Cout));
  // Probe on R

  // Notes on the sheet:
  //   00: and
  //   01: or
  //   10: add
  //   11: sub
endmodule

module NEGATIVE (
  input  [7:0] in_1,
  output [7:0] out_2
);

  wire [7:0] not_1_out;

  assign not_1_out = ~in_1;  // NOT_Gate not_1, 8 bits wide
  INC inc_1 (.X(not_1_out), .R(out_2));  // open: Cout
endmodule

module INC (
  input  [7:0] X,
  output [7:0] R,
  output Cout
);

  wire [7:1] and_1_out;

  assign {Cout, and_1_out} = {and_1_out, 1'b1} & X;  // AND_Gate and_1, 8 bits wide
  assign R = X ^ {and_1_out, 1'b1};  // XOR_Gate xor_1, 8 bits wide

  // Notes on the sheet:
  //   ИНКРЕМЕНТАТОР
endmodule
