// Logisim project NSU-2022-T06L1e01.circ as structural Verilog: 1 circuit, main circuit fib32
module fib32 (
  input  clock,
  output [31:0] a,
  output [5:0] k,
  output stop
);

  wire comparator_1_eq, controlled_buffer_1_out, controlled_buffer_2_out, not_1_out, not_2_out;
  wire [5:0] adder_2_out;
  wire [31:0] adder_1_out, multiplexer_1_out, x;

  Multiplexer #(.width(32), .enable("false")) multiplexer_1 (
    .in0(x), .in1(32'h1), .out(multiplexer_1_out), .sel(comparator_1_eq));
  Comparator #(.width(32)) comparator_1 (.a(a), .b({32{1'b0}}), .eq(comparator_1_eq));  // open: gt, lt
  Adder #(.width(32)) adder_1 (.a(a), .b(multiplexer_1_out), .out(adder_1_out), .cout(stop));  // open: cin
  not not_1 (not_1_out, stop);
  assign controlled_buffer_1_out = not_1_out ? clock : 1'bz;  // Controlled_Buffer controlled_buffer_1
  not not_2 (not_2_out, stop);
  assign controlled_buffer_2_out = not_2_out ? clock : 1'bz;  // Controlled_Buffer controlled_buffer_2
  Register #(.width(32)) register_1 (.D(adder_1_out), .Q(a), .clk(controlled_buffer_1_out));  // open: en, clr
  Adder #(.width(6)) adder_2 (.a(k), .b(6'b000001), .out(adder_2_out));  // open: cin, cout
  Register #(.width(32)) register_2 (.D(a), .Q(x), .clk(controlled_buffer_1_out));  // open: en, clr
  Register #(.width(6)) register_3 (.D(adder_2_out), .Q(k), .clk(controlled_buffer_2_out));  // open: en, clr
  // Probe on a
  // Probe on k

  // Other names for the same wires on the sheet: out[31:0] = a
endmodule
